# Fritzing sketch 2P-Battery-Board (saved by Fritzing 0.9.10b)
circuit board: 8.3026cm x 4.2732cm
breadboards: 1

parts:
  BAT1 = 18650 battery holder [package=battery-18650-kit]
  BAT2 = 18650 battery holder [package=battery-18650-kit]
  + = female pin header, 1 pin [form="♀ (female)"]
  - = female pin header, 1 pin [form="♀ (female)"]

nets:
  N1: BAT1.+, BAT2.+, +.pin1
  N2: BAT1.-, BAT2.-, -.pin1

custom parts:
  18650 battery holder: 18650 Battery
