# Fritzing sketch SpyCam (saved by Fritzing 0.9.10b)
breadboards: 1

parts:
  ESP32_-_Back1 = ESP32 - CAM
  R1 = Resistor [tolerance=±5% power=0.25 resistance=220 package=THT]
  LED1 = LED - 5mm [color="Red (633nm)" current=0.030 package="5 mm [THT]"]
  S1 = Toggle Switch [package=THT]
  BAT1 = Battery Holders [package=lipo-1100mAh]
  TP1 = TP4056 [chip_label=TP4056 package="DIP (Dual Inline) [THT]"]

nets:
  N1: ESP32_-_Back1.5V, R1.Pin_0, S1.COM
  N2: ESP32_-_Back1.3.3V, LED1.cathode, TP1.pin6
  N3: R1.Pin_1, LED1.anode
  N4: S1.L1, TP1.pin3
  N5: BAT1.+, TP1.pin4
  N6: BAT1.-, TP1.pin5

notes:
  Spy Cam, Spy Cam with ESP32-Cam, 1.0

custom parts:
  ESP32 - CAM: The ESP32-CAM has a very competitive small-size camera module that can operate independently as a minimum system with a footprint of only 27*40.5*4.5mm and a deep sleep current of up to 6mA.
  TP4056: A DIP stand-in part for whatever IC you want. With 6 pins on a 300mil dual inline package (DIP) footprint.
