# Fritzing sketch SpyCamV2 (saved by Fritzing 0.9.10b)
breadboards: 1

parts:
  ESP32_-_Back1 = ESP32 - CAM
  BAT1 = 18650 battery holder [package=battery-18650-kit]
  BAT2 = 18650 battery holder [package=battery-18650-kit]
  TP1 = TP4056 [chip_label=TP4056 package="DIP (Dual Inline) [THT]"]

nets:
  N1: ESP32_-_Back1.GND, TP1.pin3
  N2: ESP32_-_Back1.3.3V, TP1.pin6
  N3: BAT1.+, BAT2.+, TP1.pin4
  N4: BAT1.-, BAT2.-, TP1.pin5

custom parts:
  ESP32 - CAM: The ESP32-CAM has a very competitive small-size camera module that can operate independently as a minimum system with a footprint of only 27*40.5*4.5mm and a deep sleep current of up to 6mA.
  18650 battery holder: 18650 Battery
  TP4056: A DIP stand-in part for whatever IC you want. With 6 pins on a 300mil dual inline package (DIP) footprint.
